# Fritzing sketch MachineF3Iessai (saved by Fritzing 0.9.2b)
stripboards: 1

parts:
  R1 = Resistor [tolerance=±5% resistance=10k package=THT]
  R2 = Resistor [tolerance=±5% resistance=10k package=THT]
  R3 = Resistor [tolerance=±5% resistance=10k package=THT]
  R4 = Resistor [tolerance=±5% resistance=10k package=THT]
  R5 = Resistor [tolerance=±5% resistance=10k package=THT]
  J1 = screw terminal, 6 pins
  LCD1 = LCD screen  # not connected
  J2 = screw terminal, 16 pins
  J3 = screw terminal, 3 pins
  J4 = screw terminal, 8 pins
  J5 = screw terminal, 10 pins
  part = screw terminal, 10 pins  # not connected
  Composants1 = Arduino Mega 2560 (Rev3)

nets:
  N1: R1.Pin_0, R2.Pin_0, R3.Pin_0, R4.Pin_0, R5.Pin_0, J2.pin2, J2.pin15, J3.pin3, J5.pin7, Composants1.5V
  N2: R1.Pin_1, J1.pin3, Composants1.D28
  N3: R2.Pin_1, J1.pin4, Composants1.D26
  N4: R3.Pin_1, J1.pin5, Composants1.D24
  N5: R4.Pin_1, J1.pin6, Composants1.D22
  N6: R5.Pin_1, J1.pin2, Composants1.D30
  N7: J1.pin1, J2.pin1, J2.pin7, J2.pin8, J2.pin9, J2.pin10, J2.pin12, J2.pin16, J3.pin1, Composants1.GND
  N8: J2.pin3, Composants1.D52
  N9: J2.pin4, Composants1.D50
  N10: J2.pin5, Composants1.D48
  N11: J2.pin6, Composants1.D46
  N12: J2.pin11, Composants1.D44
  N13: J2.pin13, Composants1.D42
  N14: J2.pin14, J3.pin2
  N15: J4.pin1, Composants1.D38
  N16: J4.pin2, Composants1.D40
