# Fritzing sketch f3i (saved by Fritzing 0.9.3b)
circuit board: 10.4712cm x 12.8013cm
breadboards: 1
stripboards: 1

parts:
  R1 = Resistor [tolerance=±5% resistance=10k package=THT]
  R5 = Resistor [tolerance=±5% resistance=10k package=THT]
  R4 = Resistor [tolerance=±5% resistance=10k package=THT]
  R3 = Resistor [tolerance=±5% resistance=10k package=THT]
  R1_2 = Resistor [tolerance=±5% resistance=10k package=THT]
  LCD1 = LCD screen
  Xbee = XBEE-1 [package=xbee-1]
  J2 = Screw terminal - 2 pins [package=THT]
  R2 = Resistor [tolerance=±5% resistance=10k package=THT]
  R2_2 = Resistor [tolerance=±5% resistance=10k package=THT]
  P1 = screw terminal, 3 pins
  LCD = shrouded pin header, 16 pins [form="♂ (shrouded male)"]
  R6 = Resistor [tolerance=±5% resistance=220 package=THT]
  Asso = LED - 5mm [color="Red (633nm)" package="5 mm [THT]"]
  J1 = Screw terminal - 2 pins [package=THT]
  R7 = TRIMPOT [package=trimpot_pth_s3_lock]
  LCD_2 = shrouded pin header, 16 pins [form="♂ (shrouded male)"]
  Arduino_Fio = Arduino Fio (Funnel I/O)
  R6_2 = Resistor [tolerance=±5% resistance=10k package=THT]
  SWITCH = shrouded pin header, 16 pins [form="♂ (shrouded male)"]
  R7_2 = Resistor [tolerance=±5% resistance=10k package=THT]
  R8 = Resistor [tolerance=±5% resistance=10k package=THT]
  J3 = shrouded pin header, 16 pins [form="♂ (shrouded male)"]
  part = Arduino Mega 2560 (Rev3)  # not connected
  Arduino_Mega = Arduino Mega 2560 (Rev3)

nets (from the pcb view):
  N1: R1.Pin_0, R2.Pin_0, R7.CCW, LCD_2.pin8, Arduino_Fio.VCC
  N2: R1.Pin_1, J1.pin1, Arduino_Fio.D0/RXI
  N3: R5.Pin_0, R4.Pin_0, R3.Pin_0, R1_2.Pin_0, R2_2.Pin_0, P1.pin3, LCD.pin8, LCD.pin16, R6_2.Pin_0, R7_2.Pin_0, R8.Pin_0, Arduino_Mega.5V
  N4: R5.Pin_1, SWITCH.pin4, Arduino_Mega.D30
  N5: R4.Pin_1, SWITCH.pin5, Arduino_Mega.D28
  N6: R3.Pin_1, SWITCH.pin6, Arduino_Mega.D26
  N7: R1_2.Pin_1, SWITCH.pin8, Arduino_Mega.D22
  N8: LCD1.VSS, J3.pin1
  N9: LCD1.VDD, J3.pin2
  N10: LCD1.V0, J3.pin3
  N11: LCD1.RS, J3.pin4
  N12: LCD1.R/W, J3.pin5
  N13: LCD1.E, J3.pin6
  N14: LCD1.DB0, J3.pin7
  N15: LCD1.DB1, J3.pin8
  N16: LCD1.DB2, J3.pin9
  N17: LCD1.DB3, J3.pin10
  N18: LCD1.DB4, J3.pin11
  N19: LCD1.DB5, J3.pin12
  N20: LCD1.DB6, J3.pin13
  N21: LCD1.DB7, J3.pin14
  N22: LCD1.LED+, J3.pin15
  N23: LCD1.LED-, J3.pin16
  VDD: Xbee.VDD, Arduino_Mega.3V3
  N24: Xbee.DOUT, Arduino_Mega.D19/RX1
  N25: Xbee.DIN, Arduino_Mega.D18/TX1
  GND: Xbee.GND, P1.pin1, LCD.pin1, LCD.pin3, LCD.pin4, LCD.pin5, LCD.pin9, LCD.pin12, LCD.pin13, Asso.cathode, SWITCH.pin9, SWITCH.pin10, SWITCH.pin11, SWITCH.pin12, SWITCH.pin13, SWITCH.pin14, SWITCH.pin15, SWITCH.pin16, Arduino_Mega.GND
  N26: Xbee.DIO5, R6.Pin_1
  N27: Xbee.DIO2, Arduino_Mega.D5_PWM
  N28: Xbee.DIO1, Arduino_Mega.D6_PWM
  N29: Xbee.DIO0, Arduino_Mega.D7_PWM
  N30: J2.pin1, R2.Pin_1, Arduino_Fio.D1/TXO
  N31: J2.pin2, J1.pin2, R7.CW, LCD_2.pin1, LCD_2.pin3, LCD_2.pin4, LCD_2.pin5, LCD_2.pin9, LCD_2.pin12, LCD_2.pin13, Arduino_Fio.GND
  N32: R2_2.Pin_1, SWITCH.pin7, Arduino_Mega.D24
  N33: P1.pin2, LCD.pin2
  N34: LCD.pin6, Arduino_Mega.D44
  N35: LCD.pin7, Arduino_Mega.D48
  N36: LCD.pin10, Arduino_Mega.D50
  N37: LCD.pin11, Arduino_Mega.D46
  N38: LCD.pin14, Arduino_Mega.D42
  N39: LCD.pin15, Arduino_Mega.D40
  N40: R6.Pin_0, Asso.anode
  N41: R7.WIPER, LCD_2.pin2
  N42: LCD_2.pin6, Arduino_Fio.D4
  N43: LCD_2.pin7, Arduino_Fio.D6_PWM
  N44: LCD_2.pin10, Arduino_Fio.D7
  N45: LCD_2.pin11, Arduino_Fio.D5_PWM
  N46: LCD_2.pin14, Arduino_Fio.D3_PWM
  N47: LCD_2.pin15, Arduino_Fio.D2
  N48: R6_2.Pin_1, SWITCH.pin3, Arduino_Mega.D32
  N49: SWITCH.pin1, R8.Pin_1, Arduino_Mega.D36
  N50: SWITCH.pin2, R7_2.Pin_1, Arduino_Mega.D34

notes:
  TZ F3Q V2 2014
